// Logisim project Logisim Design.circ as structural Verilog
module ALU (
  input  [15:0] Input,
  input  [15:0] Input_2,
  input  [1:0] ALU_Control_Signal,
  output Zero_Signal__for_branching,
  output [15:0] Output
);

  wire [15:0] adder_1_out, and_1_out, or_1_out, subtractor_1_out;

  Adder #(.width(16)) adder_1 (.a(Input), .b(Input_2), .out(adder_1_out));  // open: cin, cout
  Subtractor #(.width(16)) subtractor_1 (.a(Input), .b(Input_2), .out(subtractor_1_out));  // open: bin, bout
  assign and_1_out = Input & Input_2;  // AND_Gate and_1, 16 bits wide
  assign or_1_out = Input | Input_2;  // OR_Gate or_1, 16 bits wide
  Multiplexer #(.select(2), .width(16), .enable("false")) multiplexer_1 (
    .in0(adder_1_out), .in1(subtractor_1_out), .in2(and_1_out), .in3(or_1_out), .out(Output),
    .sel(ALU_Control_Signal));
  nor nor_1 (Zero_Signal__for_branching, Output[15], Output[14], Output[13], Output[12], Output[11], Output[10], Output[9], Output[8], Output[7], Output[6], Output[5], Output[4], Output[3], Output[2], Output[1], Output[0]);
endmodule
